# Fritzing sketch thermometre-v3 (saved by Fritzing 0.7.10b)
breadboards: 1

parts:
  Arduino1 = Arduino
  LCD1 = LCD screen
  R1 = Resistor [tolerance=±5% resistance=220 package=THT]
  S1 = Pushbutton [package="[THT]"]
  Q1 = NPN-Transistor [package="TO92 [THT]"]
  R2 = Resistor [tolerance=±5% resistance=1k package=THT]
  J1 = Piezo Speaker
  S2 = Pushbutton [package="[THT]"]
  R3 = Resistor [tolerance=±5% resistance=220 package=THT]
  R4 = Resistor [tolerance=±5% resistance=10k package=THT]
  T1 = LM35 Temperature Sensor [package="TO92 [THT]"]
  T2 = LM35 Temperature Sensor [package="TO92 [THT]"]
  R5 = Resistor [tolerance=±5% resistance=220 package=THT]
  R6 = Resistor [tolerance=±5% resistance=220 package=THT]

nets:
  N1: Arduino1.D12, LCD1.DB7
  N2: Arduino1.D11, LCD1.DB6
  N3: Arduino1.D10, LCD1.DB5
  N4: Arduino1.D9, LCD1.DB4
  N5: Arduino1.D8, LCD1.E
  N6: Arduino1.D7, LCD1.RS
  N7: Arduino1.D6, R2.Pin_0
  N8: Arduino1.D3, J1.pin2
  N9: Arduino1.D2, R3.Pin_0, R4.Pin_0
  N10: Arduino1.A2, T1.Vout, R5.Pin_0
  N11: Arduino1.A4, T2.Vout, R6.Pin_0
  GND: LCD1.VSS, LCD1.R/W, R1.Pin_1, S1.Pin_1, S1.Pin_2, Q1.C, J1.pin1, S2.Pin_1, S2.Pin_2, T1.GND, T2.GND
  N12: LCD1.VDD, LCD1.LED+, R4.Pin_1, R5.Pin_1, R6.Pin_1
  N13: LCD1.V0, R1.Pin_0
  N14: LCD1.LED-, S1.Pin_3, S1.Pin_4, Q1.E
  N15: Q1.B, R2.Pin_1
  N16: S2.Pin_3, S2.Pin_4, R3.Pin_1

notes:
  LM_3_35
  not LM35
